# Fritzing sketch Aircon (saved by Fritzing 1.0.6)
circuit board: 8.46667cm x 5.64444cm
stripboards: 1

parts:
  R1 = Resistor [tolerance=±5% power=0.25W resistance=22k package=THT]
  R2 = Resistor [tolerance=±5% power=0.25W resistance=4.7k package=THT]
  Q1 = NPN-Transistor [package="TO92 [THT]"]
  R3 = Resistor [tolerance=±5% power=0.25W resistance=1k package=THT]
  A1 = Esp32-c3 super mini
  U4 = HW-133 DC-DC Module [part_number=HW-133]
  J2 = JST-B3B-XH-A [part_number=B3B-XH-A package=THT]
  A2 = MCP4725

nets:
  N1: R1.Pin_0, A2.pin1
  N2: R1.Pin_1, Q1.B
  N3: R2.Pin_0, U4.VCC_IN, U4.VCC_IN_(2), J2.pin1
  N4: R2.Pin_1, R3.Pin_0, A1.Pin_13
  GND: Q1.E, R3.Pin_1, A1.Pin_15, U4.GND_IN, U4.GND_IN_(2), U4.GND_OUT, U4.GND_OUT_(2), J2.pin2, A2.pin2
  N5: Q1.C, J2.pin3
  N6: A1.Pin_6, A2.pin4
  N7: A1.Pin_12, A2.pin3
  N8: A1.Pin_16, U4.VCC_OUT, U4.VCC_OUT_(2), A2.pin5

notes:
  16: 5V
  15: GND
  6: SDA
  12: SCL
  13: GPIO4
  3: Key-A
  2: COM
  1: POWER-C

custom parts:
  Esp32-c3 super mini: ESP32-C3 Development Board ESP32 SuperMini Development Board ESP32 Development Board WiFi Bluetooth.
  HW-133 DC-DC Module: HW-133 DC-DC Module Adapter with variable input/output Adapted from DSUN-DC by Bluewalk
  MCP4725: The MCP4725 is an I2C controlled Digital-to-Analog converter (DAC) based on Fritzing Part-o-matic
